# Fritzing sketch BB_Phase_2 (saved by Fritzing 0.9.2b)
breadboards: 1

parts:
  Part1 = Mikrobus - Cobbler
  Q1 = PIC32mx250f128-B [package=PDIP]
  C1 = Ceramic Capacitor [capacitance=100nF package="100 mil [THT, multilayer]"]
  R13 = Resistor [tolerance=±10% resistance=10k package=THT]
  R17 = Resistor [tolerance=±5% resistance=330 package=THT]
  C2 = Ceramic Capacitor [capacitance=100nF package="100 mil [THT, multilayer]"]
  R18 = Resistor [tolerance=±5% resistance=1k package=THT_mini]

nets:
  N1: Part1.AN, R17.Pin_0
  N2: Part1.+3.3V, Q1.13-VDD, R13.Pin_0
  N3: Part1.GND, Q1.8-VSS, Q1.19-VSS, C1.0, C2.0
  N4: Part1.SDA, Q1.18-RB9
  N5: Part1.SCL, Q1.17-RB8
  N6: Part1.TX, Q1.5-RB1
  N7: Part1.RX, Q1.4-RB0
  N8: Q1.1-MCLR, R17.Pin_1, R18.Pin_1
  N9: Q1.20-VCAP, C2.1
  N10: C1.1, R13.Pin_1, R18.Pin_0

custom parts:
  Mikrobus - Cobbler: The idea of the Mikrobus cobbler is to plug it into a breadboard and connect the 40 way connector to the 40 way connector on the Raspberry Pi B+, 2B using a Ribbon cable. You can then prototype your Mikrobus board and test with the Raspberry Pi
  PIC32mx250f128-B: PIC 32 mx250f128 B
  220 Ω Resistor: A generic resistor (0.25W)
